# Fritzing sketch fiz-2 (saved by Fritzing 0.8.3b)
breadboards: 1

parts:
  Part2 = Arduino Uno (Rev3)
  R1 = Photocell (LDR) [package=THT]
  R2 = Resistor [tolerance=±5% resistance=220 package="0603 [SMD]"]
  J1 = Basic Servo

nets:
  N1: Part2.A0, R1.pin_0, R2.Pin_1
  5V: Part2.5V, R1.pin_1, J1.vcc
  GND: Part2.GND, R2.Pin_0, J1.gnd
  N2: Part2.D9_PWM, J1.pulse
